# Fritzing sketch step2 (saved by Fritzing 0.9.3b)
breadboards: 1

parts:
  Часть1 = Arduino Nano (Rev3.0)
  Часть2 = Bluetooth HC-05 Macho
  C1 = Capacitor Polarized [package=cpol-radial-10uf-25v]
  R1 = Resistor [tolerance=±5% resistance=220 package="2512 [SMD]"]

nets:
  N1: Часть1.D1/TX, R1.Pin_0
  N2: Часть1.D0/RX, Часть2.TXD
  GND: Часть1.GND, Часть2.GND
  N3: Часть1.RESET, C1.-
  5V: Часть1.5V, Часть2.VCC
  N4: Часть2.State, C1.+
  N5: Часть2.RXD, R1.Pin_1
